// Logisim project Project1调试版 2.circ as structural Verilog: 10 circuits, main circuit main
module main (
  input  Reset
);

  wire ALU_e, ALUSrc, and_1_out, CLK, controller_and_1_add, controller_and_1_addi, controller_and_1_addiu,
       controller_and_1_addu, controller_and_1_beq, controller_and_1_j, controller_and_1_jal,
       controller_and_1_jr, controller_and_1_lb, controller_and_1_lui, controller_and_1_lw,
       controller_and_1_ori, controller_and_1_sb, controller_and_1_sll, controller_and_1_srl,
       controller_and_1_subu, controller_and_1_sw, E, IsE, IsShamt, jal, jr, lb, MemtoReg, MemWrite, RegDst,
       RegWrite, sb, Zero;
  wire [1:0] Ext_op, nPC_sel;
  wire [2:0] ALU_Ctrl;
  wire [4:0] multiplexer_2_out, multiplexer_5_out, multiplexer_6_out, rs, rt;
  wire [5:0] Funct, OpCode;
  wire [15:6] Imm_16;
  wire [23:0] ram_1_data;
  wire [31:0] A, B, C, DM_Out, ext_1_output32, jalAdd, jrNPC, multiplexer_1_out, multiplexer_3_out,
       multiplexer_4_out, multiplexer_7_out, multiplexer_8_out, multiplexer_9_out;
  wire [31:24] ram_1_data_2;

  Clock u_CLK (.out(CLK));
  LED led_1 (.in(and_1_out));
  and and_1 (and_1_out, E, IsE);
  IFU ifu_1 (
    .Zero(Zero), .Reset(Reset), .Instr_31_0({OpCode, rs, rt, Imm_16, Funct}), .CLK(CLK), .nPC_sel(nPC_sel),
    .jalOut(jalAdd), .jalEN(jal), .jr(jr), .jalNPC(jrNPC));
  Multiplexer #(.width(32), .enable("false")) multiplexer_1 (
    .in0(C), .in1(DM_Out), .out(multiplexer_1_out), .sel(MemtoReg));
  Multiplexer #(.width(5), .enable("false")) multiplexer_2 (
    .in0(rs), .in1({5{1'b0}}), .out(multiplexer_2_out), .sel(IsShamt));
  Multiplexer #(.select(2), .width(32)) multiplexer_3 (
    .in0({DM_Out[31:8], B[7:0]}), .in1({DM_Out[31:16], B[7:0], DM_Out[7:0]}),
    .in2({DM_Out[31:24], B[7:0], DM_Out[15:0]}), .in3({B[7:0], DM_Out[23:0]}), .out(multiplexer_3_out),
    .sel(Funct[1:0]), .en(sb));
  // Probe on {OpCode, rs, rt, Imm_16, Funct}
  Multiplexer #(.width(32), .enable("false")) multiplexer_4 (
    .in0(multiplexer_1_out), .in1(jalAdd), .out(multiplexer_4_out), .sel(jal));
  Multiplexer #(.width(5), .enable("false")) multiplexer_5 (
    .in0(rt), .in1(Imm_16[15:11]), .out(multiplexer_5_out), .sel(RegDst));
  Multiplexer #(.width(5), .enable("false")) multiplexer_6 (
    .in0(multiplexer_5_out), .in1({5{1'b1}}), .out(multiplexer_6_out), .sel(jal));
  // Probe on A
  GPR gpr_1 (
    .CLK(CLK), .rst(Reset), .Input(multiplexer_4_out), .RegW(RegWrite), .rw(multiplexer_6_out),
    .rs(multiplexer_2_out), .rt(rt), .A(A), .B(B));
  // Probe on B
  Multiplexer #(.width(32), .enable("false")) multiplexer_7 (
    .in0(B), .in1(multiplexer_3_out), .out(multiplexer_7_out), .sel(sb));
  // Probe on Funct
  // Probe on OpCode
  Controller_And controller_and_1 (
    .funct(Funct), .op(OpCode), .ori(controller_and_1_ori), .addu(controller_and_1_addu),
    .subu(controller_and_1_subu), .lw(controller_and_1_lw), .sw(controller_and_1_sw),
    .beq(controller_and_1_beq), .lui(controller_and_1_lui), .j(controller_and_1_j),
    .addiu(controller_and_1_addiu), .add(controller_and_1_add), .addi(controller_and_1_addi),
    .sll(controller_and_1_sll), .srl(controller_and_1_srl), .sb(controller_and_1_sb),
    .jal(controller_and_1_jal), .lb(controller_and_1_lb), .jr(controller_and_1_jr));
  EXT ext_1 (.Imm16({Imm_16, Funct}), .EXTop(Ext_op), .Output32(ext_1_output32));
  RAM #(.addrWidth(5), .dataWidth(32), .bus("separate")) ram_1 (
    .addr(C[6:2]), .din(multiplexer_7_out), .data({ram_1_data_2, ram_1_data}), .str(MemWrite), .clk(CLK));  // open: sel, ld, clr
  Controller_Or controller_or_1 (
    .ori(controller_and_1_ori), .addiu(controller_and_1_addiu), .addu(controller_and_1_addu),
    .subu(controller_and_1_subu), .lw(controller_and_1_lw), .sw(controller_and_1_sw),
    .beq(controller_and_1_beq), .lui(controller_and_1_lui), .j(controller_and_1_j), .RegDst(RegDst),
    .ALUSrc(ALUSrc), .MemtoReg(MemtoReg), .RegWrite(RegWrite), .MemWrite(MemWrite), .nPC_sel(nPC_sel),
    .ExtOp(Ext_op), .ALUctrl(ALU_Ctrl), .add(controller_and_1_add), .addi(controller_and_1_addi),
    .jal(controller_and_1_jal), .sll(controller_and_1_sll), .srl(controller_and_1_srl),
    .sb(controller_and_1_sb), .sb_2(sb), .IsE(IsE), .IsShamt(IsShamt), .lb(controller_and_1_lb), .lb_2(lb),
    .jr(controller_and_1_jr), .jr_2(jr));
  Multiplexer #(.width(32), .enable("false")) multiplexer_8 (
    .in0(B), .in1(ext_1_output32), .out(multiplexer_8_out), .sel(ALUSrc));
  // Probe on {ram_1_data_2, ram_1_data}
  ALU ALU (
    .A(A), .B(multiplexer_8_out), .shamt(Imm_16[10:6]), .ALU_Ctrl(ALU_Ctrl), .E(ALU_e), .C(C), .Zero(Zero));  // open: A_B, A_B_2
  and and_2 (jal, ~nPC_sel[0], nPC_sel[1], RegWrite);  // AND_Gate
  xor xor_1 (E, ALU_e, C[31]);
  Multiplexer #(.select(2), .width(32)) multiplexer_9 (
    .in0({B[31:8], ram_1_data[7:0]}), .in1({B[31:16], ram_1_data[15:8], B[7:0]}),
    .in2({B[31:24], ram_1_data[23:16], B[15:0]}), .in3({ram_1_data_2, B[23:0]}), .out(multiplexer_9_out),
    .sel(Funct[1:0]), .en(lb));
  // Probe on C
  Multiplexer #(.width(32), .enable("false")) multiplexer_10 (
    .in0({ram_1_data_2, ram_1_data}), .in1(multiplexer_9_out), .out(DM_Out), .sel(lb));

  // Other names for the same wires on the sheet: Imm_16[5:0] = Funct; shamt[4:0] = Imm_16[10:6];
  //   rd[4:0] = Imm_16[15:11]

  // Notes on the sheet:
  //   DM
endmodule

module ALU (
  input  [31:0] A,
  input  [31:0] B,
  input  [4:0] shamt,
  input  [2:0] ALU_Ctrl,
  output E,
  output [31:0] C,
  output A_B,
  output Zero,
  output A_B_2
);

  wire [31:0] adder_1_c, and_1_out, or_1_out, shifter_1_out, shifter_2_out, subtractor_1_c;

  adder adder_1 (.A(A), .B(B), .C(adder_1_c), .E(E));
  subtractor subtractor_1 (.A(A), .B(B), .C(subtractor_1_c));
  assign and_1_out = A & B;  // AND_Gate and_1, 32 bits wide
  assign or_1_out = A | B;  // OR_Gate or_1, 32 bits wide
  Shifter #(.width(32)) shifter_1 (.in(B), .\dist (shamt), .out(shifter_1_out));
  Shifter #(.width(32), .shift("lr")) shifter_2 (.in(B), .\dist (shamt), .out(shifter_2_out));
  Multiplexer #(.select(3), .width(32), .enable("false")) multiplexer_1 (
    .in0(adder_1_c), .in1(subtractor_1_c), .in2(and_1_out), .in3(or_1_out), .in4(shifter_1_out),
    .in5(shifter_2_out), .out(C), .sel(ALU_Ctrl));  // open: in6, in7
  Comparator #(.width(32)) comparator_1 (.a(subtractor_1_c), .b({32{1'b0}}), .gt(A_B), .eq(Zero), .lt(A_B_2));
endmodule

module IFU (
  input  Zero,
  input  [31:0] jalNPC,
  input  jr,
  input  [1:0] nPC_sel,
  input  jalEN,
  input  CLK,
  input  Reset,
  output [31:0] Instr_31_0,
  output [31:0] jalOut
);

  wire [0:0] and_1_out;
  wire [29:0] adder_2_out, bit_extender_1_out, multiplexer_1_out, multiplexer_2_out, PC_NEXT, PC_q;

  Multiplexer #(.select(2), .width(30), .enable("false")) multiplexer_1 (
    .in0(PC_NEXT), .in1(adder_2_out), .in2({PC_NEXT[29:26], Instr_31_0[25:0]}), .in3(PC_NEXT),
    .out(multiplexer_1_out), .sel({nPC_sel[1], and_1_out[0]}));
  and and_1 (and_1_out[0], Zero, nPC_sel[0]);
  Register #(.width(30)) PC (.D(multiplexer_2_out), .Q(PC_q), .clk(CLK), .clr(Reset));  // open: en
  Multiplexer #(.width(30), .enable("false")) multiplexer_2 (
    .in0(multiplexer_1_out), .in1(jalNPC[31:2]), .out(multiplexer_2_out), .sel(jr));
  Adder #(.width(30)) adder_1 (.a(PC_q), .b(30'h1), .out(PC_NEXT));  // open: cin, cout
  ROM #(.addrWidth(6), .dataWidth(32)) rom_1 (.addr(PC_q[5:0]), .data(Instr_31_0));  // open: sel
  assign bit_extender_1_out = {{14{Instr_31_0[15]}}, Instr_31_0[15:0]};  // Bit_Extender bit_extender_1
  Adder #(.width(30)) adder_2 (.a(PC_NEXT), .b(bit_extender_1_out), .out(adder_2_out));  // open: cin, cout
  assign jalOut = jalEN ? {PC_NEXT, 2'b00} : 32'bz;  // Controlled_Buffer controlled_buffer_1

  // Notes on the sheet:
  //   beq 01，j&jal 10
  //   IM
  //   contents of rom_1 (hex, n*v repeats v):
  //   20110005 20120005 2324022 11000000 c000c06 8000c08 20130009 3e00008
  //   j
  //   jal
  //   Beq
endmodule

module GPR (
  input  CLK,
  input  rst,
  input  [31:0] Input,
  input  RegW,
  input  [4:0] rw,
  input  [4:0] rs,
  input  [4:0] rt,
  output [31:0] A,
  output [31:0] B
);

  wire demultiplexer_1_out0, demultiplexer_1_out1, demultiplexer_1_out2, demultiplexer_1_out3,
       demultiplexer_1_out4, demultiplexer_1_out5, demultiplexer_1_out6, demultiplexer_1_out7,
       demultiplexer_1_out8, demultiplexer_1_out9, demultiplexer_1_out10, demultiplexer_1_out11,
       demultiplexer_1_out12, demultiplexer_1_out13, demultiplexer_1_out14, demultiplexer_1_out15,
       demultiplexer_1_out16, demultiplexer_1_out17, demultiplexer_1_out18, demultiplexer_1_out19,
       demultiplexer_1_out20, demultiplexer_1_out21, demultiplexer_1_out22, demultiplexer_1_out23,
       demultiplexer_1_out24, demultiplexer_1_out25, demultiplexer_1_out26, demultiplexer_1_out27,
       demultiplexer_1_out28, demultiplexer_1_out29, demultiplexer_1_out30, demultiplexer_1_out31;
  wire [31:0] _0, _1, _2, _3, _4, _5, _6, _7, _8, _9, _10, _11, _12, _13, _14, _15, _16, _17, _18, _19, _20,
       _21, _22, _23, _24, _25, _26, _27, _28, _29, _30, _31;

  Demultiplexer #(.select(5), .enable("false")) demultiplexer_1 (
    .out0(demultiplexer_1_out0), .out1(demultiplexer_1_out1), .out2(demultiplexer_1_out2),
    .out3(demultiplexer_1_out3), .out4(demultiplexer_1_out4), .out5(demultiplexer_1_out5),
    .out6(demultiplexer_1_out6), .out7(demultiplexer_1_out7), .out8(demultiplexer_1_out8),
    .out9(demultiplexer_1_out9), .out10(demultiplexer_1_out10), .out11(demultiplexer_1_out11),
    .out12(demultiplexer_1_out12), .out13(demultiplexer_1_out13), .out14(demultiplexer_1_out14),
    .out15(demultiplexer_1_out15), .out16(demultiplexer_1_out16), .out17(demultiplexer_1_out17),
    .out18(demultiplexer_1_out18), .out19(demultiplexer_1_out19), .out20(demultiplexer_1_out20),
    .out21(demultiplexer_1_out21), .out22(demultiplexer_1_out22), .out23(demultiplexer_1_out23),
    .out24(demultiplexer_1_out24), .out25(demultiplexer_1_out25), .out26(demultiplexer_1_out26),
    .out27(demultiplexer_1_out27), .out28(demultiplexer_1_out28), .out29(demultiplexer_1_out29),
    .out30(demultiplexer_1_out30), .out31(demultiplexer_1_out31), .in(RegW), .sel(rw));
  Register #(.width(32)) u__0 (.D({32{1'b0}}), .en(demultiplexer_1_out0), .Q(_0), .clk(CLK), .clr(rst));
  Register #(.width(32)) register_1 (.D(Input), .en(demultiplexer_1_out1), .Q(_1), .clk(CLK), .clr(rst));
  Register #(.width(32)) u__16 (.D(Input), .en(demultiplexer_1_out16), .Q(_16), .clk(CLK), .clr(rst));
  Register #(.width(32)) register_2 (.D(Input), .en(demultiplexer_1_out2), .Q(_2), .clk(CLK), .clr(rst));
  Register #(.width(32)) register_3 (.D(Input), .en(demultiplexer_1_out17), .Q(_17), .clk(CLK), .clr(rst));
  Register #(.width(32)) register_4 (.D(Input), .en(demultiplexer_1_out3), .Q(_3), .clk(CLK), .clr(rst));
  Register #(.width(32)) register_5 (.D(Input), .en(demultiplexer_1_out18), .Q(_18), .clk(CLK), .clr(rst));
  Register #(.width(32)) register_6 (.D(Input), .en(demultiplexer_1_out4), .Q(_4), .clk(CLK), .clr(rst));
  Register #(.width(32)) register_7 (.D(Input), .en(demultiplexer_1_out19), .Q(_19), .clk(CLK), .clr(rst));
  Multiplexer #(.select(5), .width(32), .enable("false")) multiplexer_1 (
    .in0(_0), .in1(_1), .in2(_2), .in3(_3), .in4(_4), .in5(_5), .in6(_6), .in7(_7), .in8(_8), .in9(_9),
    .in10(_10), .in11(_11), .in12(_12), .in13(_13), .in14(_14), .in15(_15), .in16(_16), .in17(_17),
    .in18(_18), .in19(_19), .in20(_20), .in21(_21), .in22(_22), .in23(_23), .in24(_24), .in25(_25),
    .in26(_26), .in27(_27), .in28(_28), .in29(_29), .in30(_30), .in31(_31), .out(A), .sel(rs));
  Register #(.width(32)) register_8 (.D(Input), .en(demultiplexer_1_out5), .Q(_5), .clk(CLK), .clr(rst));
  Register #(.width(32)) register_9 (.D(Input), .en(demultiplexer_1_out20), .Q(_20), .clk(CLK), .clr(rst));
  Register #(.width(32)) register_10 (.D(Input), .en(demultiplexer_1_out6), .Q(_6), .clk(CLK), .clr(rst));
  Register #(.width(32)) register_11 (.D(Input), .en(demultiplexer_1_out21), .Q(_21), .clk(CLK), .clr(rst));
  Register #(.width(32)) u__7 (.D(Input), .en(demultiplexer_1_out7), .Q(_7), .clk(CLK), .clr(rst));
  Register #(.width(32)) register_12 (.D(Input), .en(demultiplexer_1_out22), .Q(_22), .clk(CLK), .clr(rst));
  Register #(.width(32)) u__8 (.D(Input), .en(demultiplexer_1_out8), .Q(_8), .clk(CLK), .clr(rst));
  Register #(.width(32)) u__15 (.D(Input), .en(demultiplexer_1_out23), .Q(_23), .clk(CLK), .clr(rst));
  Register #(.width(32)) register_13 (.D(Input), .en(demultiplexer_1_out9), .Q(_9), .clk(CLK), .clr(rst));
  Register #(.width(32)) _16_2 (.D(Input), .en(demultiplexer_1_out24), .Q(_24), .clk(CLK), .clr(rst));
  Register #(.width(32)) register_14 (.D(Input), .en(demultiplexer_1_out10), .Q(_10), .clk(CLK), .clr(rst));
  Register #(.width(32)) register_15 (.D(Input), .en(demultiplexer_1_out25), .Q(_25), .clk(CLK), .clr(rst));
  Register #(.width(32)) register_16 (.D(Input), .en(demultiplexer_1_out11), .Q(_11), .clk(CLK), .clr(rst));
  Register #(.width(32)) register_17 (.D(Input), .en(demultiplexer_1_out26), .Q(_26), .clk(CLK), .clr(rst));
  Register #(.width(32)) register_18 (.D(Input), .en(demultiplexer_1_out12), .Q(_12), .clk(CLK), .clr(rst));
  Register #(.width(32)) register_19 (.D(Input), .en(demultiplexer_1_out27), .Q(_27), .clk(CLK), .clr(rst));
  Multiplexer #(.select(5), .width(32), .enable("false")) multiplexer_2 (
    .in0(_0), .in1(_1), .in2(_2), .in3(_3), .in4(_4), .in5(_5), .in6(_6), .in7(_7), .in8(_8), .in9(_9),
    .in10(_10), .in11(_11), .in12(_12), .in13(_13), .in14(_14), .in15(_15), .in16(_16), .in17(_17),
    .in18(_18), .in19(_19), .in20(_20), .in21(_21), .in22(_22), .in23(_23), .in24(_24), .in25(_25),
    .in26(_26), .in27(_27), .in28(_28), .in29(_29), .in30(_30), .in31(_31), .out(B), .sel(rt));
  Register #(.width(32)) register_20 (.D(Input), .en(demultiplexer_1_out13), .Q(_13), .clk(CLK), .clr(rst));
  Register #(.width(32)) register_21 (.D(Input), .en(demultiplexer_1_out28), .Q(_28), .clk(CLK), .clr(rst));
  Register #(.width(32)) register_22 (.D(Input), .en(demultiplexer_1_out14), .Q(_14), .clk(CLK), .clr(rst));
  Register #(.width(32)) register_23 (.D(Input), .en(demultiplexer_1_out29), .Q(_29), .clk(CLK), .clr(rst));
  Register #(.width(32)) _15_2 (.D(Input), .en(demultiplexer_1_out15), .Q(_15), .clk(CLK), .clr(rst));
  Register #(.width(32)) register_24 (.D(Input), .en(demultiplexer_1_out30), .Q(_30), .clk(CLK), .clr(rst));
  Register #(.width(32)) u__31 (.D(Input), .en(demultiplexer_1_out31), .Q(_31), .clk(CLK), .clr(rst));
endmodule

module EXT (
  input  [15:0] Imm16,
  input  [1:0] EXTop,
  output [31:0] Output32
);

  wire [15:0] demultiplexer_1_out0, demultiplexer_1_out1, demultiplexer_1_out2;
  wire [31:0] bit_extender_1_out, bit_extender_2_out;

  Demultiplexer #(.select(2), .width(16), .enable("false")) demultiplexer_1 (
    .out0(demultiplexer_1_out0), .out1(demultiplexer_1_out1), .out2(demultiplexer_1_out2), .in(Imm16),
    .sel(EXTop));  // open: out3
  assign bit_extender_1_out = {{16{1'b0}}, demultiplexer_1_out0};  // Bit_Extender bit_extender_1
  assign bit_extender_2_out = {{16{demultiplexer_1_out1[15]}}, demultiplexer_1_out1};  // Bit_Extender bit_extender_2
  Multiplexer #(.select(2), .width(32), .enable("false")) multiplexer_1 (
    .in0(bit_extender_1_out), .in1(bit_extender_2_out), .in2({demultiplexer_1_out2, {16{1'b0}}}),
    .out(Output32), .sel(EXTop));  // open: in3
endmodule

module full_Adder (
  input  a_i,
  input  b_i,
  input  c_i_1,
  output s_i,
  output c_i
);

  wire and_1_out, and_2_out, xor_1_out;

  and and_1 (and_1_out, a_i, b_i);
  xor xor_1 (xor_1_out, a_i, b_i);
  xor xor_2 (s_i, xor_1_out, c_i_1);
  and and_2 (and_2_out, xor_1_out, c_i_1);
  or or_1 (c_i, and_2_out, and_1_out);
endmodule

module adder (
  input  [31:0] A,
  input  [31:0] B,
  output E,
  output [31:0] C
);

  wire full_adder_1_c_i, full_adder_2_c_i, full_adder_3_c_i, full_adder_4_c_i, full_adder_5_c_i,
       full_adder_6_c_i, full_adder_7_c_i, full_adder_8_c_i, full_adder_9_c_i, full_adder_10_c_i,
       full_adder_11_c_i, full_adder_12_c_i, full_adder_13_c_i, full_adder_14_c_i, full_adder_15_c_i,
       full_adder_16_c_i, full_adder_17_c_i, full_adder_18_c_i, full_adder_19_c_i, full_adder_20_c_i,
       full_adder_21_c_i, full_adder_22_c_i, full_adder_23_c_i, full_adder_24_c_i, full_adder_25_c_i,
       full_adder_26_c_i, full_adder_27_c_i, full_adder_28_c_i, full_adder_29_c_i, full_adder_30_c_i,
       full_adder_31_c_i;

  full_Adder full_adder_1 (.a_i(B[0]), .b_i(A[0]), .c_i_1(1'b0), .s_i(C[0]), .c_i(full_adder_1_c_i));
  full_Adder full_adder_2 (.a_i(B[8]), .b_i(A[8]), .c_i_1(full_adder_26_c_i), .s_i(C[8]), .c_i(full_adder_2_c_i));
  full_Adder full_adder_3 (.a_i(B[16]), .b_i(A[16]), .c_i_1(full_adder_28_c_i), .s_i(C[16]), .c_i(full_adder_3_c_i));
  full_Adder full_adder_4 (.a_i(B[24]), .b_i(A[24]), .c_i_1(full_adder_31_c_i), .s_i(C[24]), .c_i(full_adder_4_c_i));
  full_Adder full_adder_5 (.a_i(B[1]), .b_i(A[1]), .c_i_1(full_adder_1_c_i), .s_i(C[1]), .c_i(full_adder_5_c_i));
  full_Adder full_adder_6 (.a_i(B[9]), .b_i(A[9]), .c_i_1(full_adder_2_c_i), .s_i(C[9]), .c_i(full_adder_6_c_i));
  full_Adder full_adder_7 (.a_i(B[17]), .b_i(A[17]), .c_i_1(full_adder_3_c_i), .s_i(C[17]), .c_i(full_adder_7_c_i));
  full_Adder full_adder_8 (.a_i(B[25]), .b_i(A[25]), .c_i_1(full_adder_4_c_i), .s_i(C[25]), .c_i(full_adder_8_c_i));
  full_Adder full_adder_9 (.a_i(B[2]), .b_i(A[2]), .c_i_1(full_adder_5_c_i), .s_i(C[2]), .c_i(full_adder_9_c_i));
  full_Adder full_adder_10 (.a_i(B[10]), .b_i(A[10]), .c_i_1(full_adder_6_c_i), .s_i(C[10]), .c_i(full_adder_10_c_i));
  full_Adder full_adder_11 (.a_i(B[3]), .b_i(A[3]), .c_i_1(full_adder_9_c_i), .s_i(C[3]), .c_i(full_adder_11_c_i));
  full_Adder full_adder_12 (.a_i(B[11]), .b_i(A[11]), .c_i_1(full_adder_10_c_i), .s_i(C[11]), .c_i(full_adder_12_c_i));
  full_Adder full_adder_13 (.a_i(B[18]), .b_i(A[18]), .c_i_1(full_adder_7_c_i), .s_i(C[18]), .c_i(full_adder_13_c_i));
  full_Adder full_adder_14 (.a_i(B[26]), .b_i(A[26]), .c_i_1(full_adder_8_c_i), .s_i(C[26]), .c_i(full_adder_14_c_i));
  full_Adder full_adder_15 (.a_i(B[4]), .b_i(A[4]), .c_i_1(full_adder_11_c_i), .s_i(C[4]), .c_i(full_adder_15_c_i));
  full_Adder full_adder_16 (.a_i(B[19]), .b_i(A[19]), .c_i_1(full_adder_13_c_i), .s_i(C[19]), .c_i(full_adder_16_c_i));
  full_Adder full_adder_17 (.a_i(B[27]), .b_i(A[27]), .c_i_1(full_adder_14_c_i), .s_i(C[27]), .c_i(full_adder_17_c_i));
  full_Adder full_adder_18 (.a_i(B[5]), .b_i(A[5]), .c_i_1(full_adder_15_c_i), .s_i(C[5]), .c_i(full_adder_18_c_i));
  full_Adder full_adder_19 (.a_i(B[12]), .b_i(A[12]), .c_i_1(full_adder_12_c_i), .s_i(C[12]), .c_i(full_adder_19_c_i));
  full_Adder full_adder_20 (.a_i(B[20]), .b_i(A[20]), .c_i_1(full_adder_16_c_i), .s_i(C[20]), .c_i(full_adder_20_c_i));
  full_Adder full_adder_21 (.a_i(B[28]), .b_i(A[28]), .c_i_1(full_adder_17_c_i), .s_i(C[28]), .c_i(full_adder_21_c_i));
  full_Adder full_adder_22 (.a_i(B[6]), .b_i(A[6]), .c_i_1(full_adder_18_c_i), .s_i(C[6]), .c_i(full_adder_22_c_i));
  full_Adder full_adder_23 (.a_i(B[13]), .b_i(A[13]), .c_i_1(full_adder_19_c_i), .s_i(C[13]), .c_i(full_adder_23_c_i));
  full_Adder full_adder_24 (.a_i(B[21]), .b_i(A[21]), .c_i_1(full_adder_20_c_i), .s_i(C[21]), .c_i(full_adder_24_c_i));
  full_Adder full_adder_25 (.a_i(B[29]), .b_i(A[29]), .c_i_1(full_adder_21_c_i), .s_i(C[29]), .c_i(full_adder_25_c_i));
  full_Adder full_adder_26 (.a_i(B[7]), .b_i(A[7]), .c_i_1(full_adder_22_c_i), .s_i(C[7]), .c_i(full_adder_26_c_i));
  full_Adder full_adder_27 (.a_i(B[14]), .b_i(A[14]), .c_i_1(full_adder_23_c_i), .s_i(C[14]), .c_i(full_adder_27_c_i));
  full_Adder full_adder_28 (.a_i(B[15]), .b_i(A[15]), .c_i_1(full_adder_27_c_i), .s_i(C[15]), .c_i(full_adder_28_c_i));
  full_Adder full_adder_29 (.a_i(B[22]), .b_i(A[22]), .c_i_1(full_adder_24_c_i), .s_i(C[22]), .c_i(full_adder_29_c_i));
  full_Adder full_adder_30 (.a_i(B[30]), .b_i(A[30]), .c_i_1(full_adder_25_c_i), .s_i(C[30]), .c_i(full_adder_30_c_i));
  full_Adder full_adder_31 (.a_i(B[23]), .b_i(A[23]), .c_i_1(full_adder_29_c_i), .s_i(C[23]), .c_i(full_adder_31_c_i));
  full_Adder full_adder_32 (.a_i(B[31]), .b_i(A[31]), .c_i_1(full_adder_30_c_i), .s_i(C[31]), .c_i(E));
endmodule

module subtractor (
  input  [31:0] A,
  input  [31:0] B,
  output [31:0] C
);

  wire [31:0] adder_1_c, not_1_out;

  assign not_1_out = ~B;  // NOT_Gate not_1, 32 bits wide
  adder adder_1 (.A(not_1_out), .B(32'h1), .C(adder_1_c));  // open: E
  adder adder_2 (.A(A), .B(adder_1_c), .C(C));  // open: E
endmodule

// Ctrl_And
module Controller_And (
  input  [5:0] funct,
  input  [5:0] op,
  output ori,
  output addiu,
  output add,
  output addi,
  output addu,
  output subu,
  output lw,
  output sw,
  output beq,
  output lui,
  output j,
  output jal,
  output sll,
  output srl,
  output sb,
  output lb,
  output jr
);

  wire not_1_out, not_2_out, not_3_out, not_4_out, not_5_out, not_6_out, not_7_out, not_8_out, not_9_out,
       not_10_out, not_11_out, not_12_out;

  not not_1 (not_1_out, funct[5]);
  not not_2 (not_2_out, funct[3]);
  not not_3 (not_3_out, funct[4]);
  not not_4 (not_4_out, funct[1]);
  not not_5 (not_5_out, funct[2]);
  not not_6 (not_6_out, funct[0]);
  not not_7 (not_7_out, op[5]);
  not not_8 (not_8_out, op[3]);
  not not_9 (not_9_out, op[4]);
  not not_10 (not_10_out, op[2]);
  not not_11 (not_11_out, op[1]);
  not not_12 (not_12_out, op[0]);
  and u_ori (ori, not_7_out, not_9_out, op[3], op[2], not_11_out, op[0]);
  and u_addiu (addiu, not_7_out, not_9_out, op[3], not_10_out, not_11_out, op[0]);
  and u_add (add, funct[5], not_3_out, not_2_out, not_5_out, not_4_out, not_6_out, not_7_out, not_9_out, not_8_out, not_10_out, not_11_out, not_12_out);
  and u_addi (addi, not_7_out, not_9_out, op[3], not_10_out, not_11_out, not_12_out);
  and u_addu (addu, not_7_out, not_9_out, not_8_out, not_10_out, not_11_out, not_12_out, funct[5], not_3_out, not_2_out, not_5_out, not_4_out, funct[0]);
  and u_subu (subu, not_7_out, not_9_out, not_8_out, not_10_out, not_11_out, not_12_out, funct[5], not_3_out, not_2_out, not_5_out, funct[1], funct[0]);
  and u_lw (lw, op[5], not_9_out, not_8_out, not_10_out, op[1], op[0]);
  and u_sw (sw, op[5], not_9_out, op[3], not_10_out, op[1], op[0]);
  and u_beq (beq, not_7_out, not_9_out, not_8_out, op[2], not_11_out, not_12_out);
  and u_lui (lui, not_7_out, not_9_out, op[3], op[2], op[1], op[0]);
  and u_j (j, not_7_out, not_9_out, not_8_out, not_10_out, op[1], not_12_out);
  and u_jal (jal, not_7_out, not_9_out, not_8_out, not_10_out, op[1], op[0]);
  and u_sll (sll, not_1_out, not_3_out, not_2_out, not_5_out, not_4_out, not_6_out, not_7_out, not_9_out, not_8_out, not_10_out, not_11_out, not_12_out);
  and u_srl (srl, not_1_out, not_3_out, not_2_out, not_5_out, funct[1], not_6_out, not_7_out, not_9_out, not_8_out, not_10_out, not_11_out, not_12_out);
  and u_sb (sb, op[5], not_9_out, op[3], not_10_out, not_11_out, not_12_out);
  and u_lb (lb, op[5], not_9_out, not_8_out, not_10_out, not_11_out, not_12_out);
  and u_jr (jr, not_1_out, not_3_out, funct[3], not_5_out, not_4_out, not_6_out, not_7_out, not_9_out, not_8_out, not_10_out, not_11_out, not_12_out);
endmodule

// Ctrl_Or
module Controller_Or (
  input  ori,
  input  addiu,
  input  add,
  input  addi,
  input  addu,
  input  subu,
  input  lw,
  input  sw,
  input  beq,
  input  lui,
  input  j,
  input  jal,
  input  sll,
  input  srl,
  input  sb,
  input  lb,
  input  jr,
  output IsE,
  output sb_2,
  output lb_2,
  output IsShamt,
  output jr_2,
  output RegDst,
  output ALUSrc,
  output MemtoReg,
  output RegWrite,
  output MemWrite,
  output [1:0] nPC_sel,
  output [1:0] ExtOp,
  output [2:0] ALUctrl
);

  or or_1 (RegDst, add, addu, subu, sll, srl);
  or or_2 (ALUSrc, lw, ori, addiu, addi, jal, sw, lui, sb, lb);
  or or_3 (MemtoReg, lw, lb);
  or or_4 (RegWrite, ori, addiu, add, addi, addu, lb, subu, lw, lui, sll, srl, jal);
  or or_5 (MemWrite, sw, sb);
  or or_6 (nPC_sel[1], j, jal);
  or or_7 (ExtOp[0], addi, lw, lb, sw, sb);
  or or_8 (ALUctrl[2], 1'b0, sll, srl);
  or or_9 (ALUctrl[1], lui, ori);
  or or_10 (ALUctrl[0], lui, beq, srl, subu, ori);
  or or_11 (IsE, add, addi);
  or or_12 (IsShamt, sll, srl);

  assign ExtOp[1] = lui;
  assign jr_2 = jr;
  assign lb_2 = lb;
  assign nPC_sel[0] = beq;
  assign sb_2 = sb;
endmodule
