// Logisim project project1单架构版 .circ as structural Verilog: 10 circuits, main circuit main
module main (
  input  in_1
);

  wire ALUsrc, beq, clk, j, MemtoReg, MemWrite, RegDst, RegWrite, sb, Zero;
  wire [1:0] ALUctr, ExtOp;
  wire [4:0] multiplexer_1_out, rs, rt;
  wire [5:0] funct, Opc;
  wire [7:0] ram_1_data, ram_1_data_2, ram_1_data_3;
  wire [15:0] regfile_1_busb_2;
  wire [15:6] imm16;
  wire [31:0] alu_1_out_alu, extener_1_out_extener, multiplexer_2_out, multiplexer_3_out, multiplexer_4_out,
       multiplexer_5_out, regfile_1_busa;
  wire [31:8] regfile_1_busb;

  // Probe on {Opc, rs, rt, imm16, funct}
  IFU ifu_1 (.j(j), .Zero(Zero), .clk(clk), .reset(in_1), .ifu_out({Opc, rs, rt, imm16, funct}));
  Controller controller_1 (
    .FUNCT(funct), .Op(Opc), .RegDst(RegDst), .ALUSrc(ALUsrc), .MemtoReg(MemtoReg), .RegWrite(RegWrite),
    .MemWrite(MemWrite), .j(j), .ExtOp(ExtOp), .ALUctr(ALUctr), .beq(beq), .sb(sb));
  Multiplexer #(.width(5), .enable("false")) multiplexer_1 (
    .in0(rt), .in1(imm16[15:11]), .out(multiplexer_1_out), .sel(RegDst));
  // Probe on multiplexer_4_out
  // Probe on funct[1:0]
  RegFile regfile_1 (
    .rs(rs), .rt(rt), .rw(multiplexer_1_out), .busW(multiplexer_5_out),
    .busB({regfile_1_busb, regfile_1_busb_2[15:8]}), .busA(regfile_1_busa), .RegW(RegWrite), .clk(clk),
    .reset(in_1));
  Extener extener_1 (.in_Extener({imm16, funct}), .ExtOp(ExtOp), .out_Extener(extener_1_out_extener));
  Clock clock_1 (.out(clk));
  Multiplexer #(.width(32), .enable("false")) multiplexer_2 (
    .in0({regfile_1_busb, regfile_1_busb_2[15:8]}), .in1(multiplexer_4_out), .out(multiplexer_2_out), .sel(sb));
  Multiplexer #(.width(32), .enable("false")) multiplexer_3 (
    .in0({regfile_1_busb, regfile_1_busb_2[15:8]}), .in1(extener_1_out_extener), .out(multiplexer_3_out),
    .sel(ALUsrc));
  ALU alu_1 (
    .in_ALU_1(regfile_1_busa), .in_ALU_2(multiplexer_3_out), .beq(beq), .ALUctr(ALUctr), .ZERO(Zero),
    .out_ALU(alu_1_out_alu));
  Multiplexer #(.select(2), .width(32)) multiplexer_4 (
    .in0({ram_1_data_3, ram_1_data_2, ram_1_data, regfile_1_busb_2[15:8]}),
    .in1({ram_1_data_3, ram_1_data_2, regfile_1_busb_2}),
    .in2({ram_1_data_3, regfile_1_busb_2[15:8], ram_1_data, regfile_1_busb_2[7:0]}),
    .in3({regfile_1_busb_2[15:8], ram_1_data_2, ram_1_data, regfile_1_busb_2[7:0]}), .out(multiplexer_4_out),
    .sel(funct[1:0]), .en(sb));
  RAM #(.addrWidth(5), .dataWidth(32), .bus("separate")) ram_1 (
    .addr(alu_1_out_alu[6:2]), .din(multiplexer_2_out),
    .data({ram_1_data_3, ram_1_data_2, ram_1_data, regfile_1_busb_2[7:0]}), .str(MemWrite), .clk(clk));  // open: sel, ld, clr
  // Probe on {ram_1_data_3, ram_1_data_2, ram_1_data, regfile_1_busb_2[7:0]}
  Multiplexer #(.width(32), .enable("false")) multiplexer_5 (
    .in0(alu_1_out_alu), .in1({ram_1_data_3, ram_1_data_2, ram_1_data, regfile_1_busb_2[7:0]}),
    .out(multiplexer_5_out), .sel(MemtoReg));

  // Other names for the same wires on the sheet: imm16[5:0] = funct; rd[4:0] = imm16[15:11]; reset = in_1
endmodule

module ADD_1bit (
  input  A_i,
  input  B_1,
  input  C_i,
  output R_i,
  output C_1_1
);

  wire and_1_out, and_2_out, and_3_out;

  xor xor_1 (R_i, A_i, B_1, C_i);
  and and_1 (and_1_out, A_i, C_i);
  and and_2 (and_2_out, A_i, B_1);
  and and_3 (and_3_out, B_1, C_i);
  or or_1 (C_1_1, and_1_out, and_2_out, and_3_out);
endmodule

// ADD
module _32bit_ADDer (
  input  [31:0] AA,
  input  [31:0] BB,
  output [31:0] RR
);

  wire add_1bit_1_c_1_1, add_1bit_2_c_1_1, add_1bit_3_c_1_1, add_1bit_4_c_1_1, add_1bit_5_c_1_1,
       add_1bit_6_c_1_1, add_1bit_7_c_1_1, add_1bit_8_c_1_1, add_1bit_9_c_1_1, add_1bit_10_c_1_1,
       add_1bit_11_c_1_1, add_1bit_12_c_1_1, add_1bit_13_c_1_1, add_1bit_14_c_1_1, add_1bit_15_c_1_1,
       add_1bit_16_c_1_1, add_1bit_17_c_1_1, add_1bit_18_c_1_1, add_1bit_20_c_1_1, add_1bit_21_c_1_1,
       add_1bit_22_c_1_1, add_1bit_23_c_1_1, add_1bit_24_c_1_1, add_1bit_25_c_1_1, add_1bit_26_c_1_1,
       add_1bit_27_c_1_1, add_1bit_28_c_1_1, add_1bit_29_c_1_1, add_1bit_30_c_1_1, add_1bit_31_c_1_1,
       n1bit_adder_1_c;

  _1bit_ADDer u_1bit_adder_1 (.A(AA[0]), .B(BB[0]), .R(RR[0]), .C(n1bit_adder_1_c));
  ADD_1bit add_1bit_1 (.B_1(BB[9]), .C_i(add_1bit_29_c_1_1), .A_i(AA[9]), .R_i(RR[9]), .C_1_1(add_1bit_1_c_1_1));
  ADD_1bit add_1bit_2 (.B_1(BB[18]), .C_i(add_1bit_30_c_1_1), .A_i(AA[18]), .R_i(RR[18]), .C_1_1(add_1bit_2_c_1_1));
  ADD_1bit add_1bit_3 (.B_1(BB[27]), .C_i(add_1bit_31_c_1_1), .A_i(AA[27]), .R_i(RR[27]), .C_1_1(add_1bit_3_c_1_1));
  ADD_1bit add_1bit_4 (.B_1(BB[1]), .C_i(n1bit_adder_1_c), .A_i(AA[1]), .R_i(RR[1]), .C_1_1(add_1bit_4_c_1_1));
  ADD_1bit add_1bit_5 (.B_1(BB[10]), .C_i(add_1bit_1_c_1_1), .A_i(AA[10]), .R_i(RR[10]), .C_1_1(add_1bit_5_c_1_1));
  ADD_1bit add_1bit_6 (.B_1(BB[19]), .C_i(add_1bit_2_c_1_1), .A_i(AA[19]), .R_i(RR[19]), .C_1_1(add_1bit_6_c_1_1));
  ADD_1bit add_1bit_7 (.B_1(BB[28]), .C_i(add_1bit_3_c_1_1), .A_i(AA[28]), .R_i(RR[28]), .C_1_1(add_1bit_7_c_1_1));
  ADD_1bit add_1bit_8 (.B_1(BB[2]), .C_i(add_1bit_4_c_1_1), .A_i(AA[2]), .R_i(RR[2]), .C_1_1(add_1bit_8_c_1_1));
  ADD_1bit add_1bit_9 (.B_1(BB[11]), .C_i(add_1bit_5_c_1_1), .A_i(AA[11]), .R_i(RR[11]), .C_1_1(add_1bit_9_c_1_1));
  ADD_1bit add_1bit_10 (.B_1(BB[20]), .C_i(add_1bit_6_c_1_1), .A_i(AA[20]), .R_i(RR[20]), .C_1_1(add_1bit_10_c_1_1));
  ADD_1bit add_1bit_11 (.B_1(BB[29]), .C_i(add_1bit_7_c_1_1), .A_i(AA[29]), .R_i(RR[29]), .C_1_1(add_1bit_11_c_1_1));
  ADD_1bit add_1bit_12 (.B_1(BB[3]), .C_i(add_1bit_8_c_1_1), .A_i(AA[3]), .R_i(RR[3]), .C_1_1(add_1bit_12_c_1_1));
  ADD_1bit add_1bit_13 (.B_1(BB[12]), .C_i(add_1bit_9_c_1_1), .A_i(AA[12]), .R_i(RR[12]), .C_1_1(add_1bit_13_c_1_1));
  ADD_1bit add_1bit_14 (.B_1(BB[21]), .C_i(add_1bit_10_c_1_1), .A_i(AA[21]), .R_i(RR[21]), .C_1_1(add_1bit_14_c_1_1));
  ADD_1bit add_1bit_15 (.B_1(BB[30]), .C_i(add_1bit_11_c_1_1), .A_i(AA[30]), .R_i(RR[30]), .C_1_1(add_1bit_15_c_1_1));
  ADD_1bit add_1bit_16 (.B_1(BB[4]), .C_i(add_1bit_12_c_1_1), .A_i(AA[4]), .R_i(RR[4]), .C_1_1(add_1bit_16_c_1_1));
  ADD_1bit add_1bit_17 (.B_1(BB[13]), .C_i(add_1bit_13_c_1_1), .A_i(AA[13]), .R_i(RR[13]), .C_1_1(add_1bit_17_c_1_1));
  ADD_1bit add_1bit_18 (.B_1(BB[22]), .C_i(add_1bit_14_c_1_1), .A_i(AA[22]), .R_i(RR[22]), .C_1_1(add_1bit_18_c_1_1));
  ADD_1bit add_1bit_19 (.B_1(BB[31]), .C_i(add_1bit_15_c_1_1), .A_i(AA[31]), .R_i(RR[31]));  // open: C_1_1
  ADD_1bit add_1bit_20 (.B_1(BB[5]), .C_i(add_1bit_16_c_1_1), .A_i(AA[5]), .R_i(RR[5]), .C_1_1(add_1bit_20_c_1_1));
  ADD_1bit add_1bit_21 (.B_1(BB[14]), .C_i(add_1bit_17_c_1_1), .A_i(AA[14]), .R_i(RR[14]), .C_1_1(add_1bit_21_c_1_1));
  ADD_1bit add_1bit_22 (.B_1(BB[23]), .C_i(add_1bit_18_c_1_1), .A_i(AA[23]), .R_i(RR[23]), .C_1_1(add_1bit_22_c_1_1));
  ADD_1bit add_1bit_23 (.B_1(BB[6]), .C_i(add_1bit_20_c_1_1), .A_i(AA[6]), .R_i(RR[6]), .C_1_1(add_1bit_23_c_1_1));
  ADD_1bit add_1bit_24 (.B_1(BB[15]), .C_i(add_1bit_21_c_1_1), .A_i(AA[15]), .R_i(RR[15]), .C_1_1(add_1bit_24_c_1_1));
  ADD_1bit add_1bit_25 (.B_1(BB[24]), .C_i(add_1bit_22_c_1_1), .A_i(AA[24]), .R_i(RR[24]), .C_1_1(add_1bit_25_c_1_1));
  ADD_1bit add_1bit_26 (.B_1(BB[7]), .C_i(add_1bit_23_c_1_1), .A_i(AA[7]), .R_i(RR[7]), .C_1_1(add_1bit_26_c_1_1));
  ADD_1bit add_1bit_27 (.B_1(BB[16]), .C_i(add_1bit_24_c_1_1), .A_i(AA[16]), .R_i(RR[16]), .C_1_1(add_1bit_27_c_1_1));
  ADD_1bit add_1bit_28 (.B_1(BB[25]), .C_i(add_1bit_25_c_1_1), .A_i(AA[25]), .R_i(RR[25]), .C_1_1(add_1bit_28_c_1_1));
  ADD_1bit add_1bit_29 (.B_1(BB[8]), .C_i(add_1bit_26_c_1_1), .A_i(AA[8]), .R_i(RR[8]), .C_1_1(add_1bit_29_c_1_1));
  ADD_1bit add_1bit_30 (.B_1(BB[17]), .C_i(add_1bit_27_c_1_1), .A_i(AA[17]), .R_i(RR[17]), .C_1_1(add_1bit_30_c_1_1));
  ADD_1bit add_1bit_31 (.B_1(BB[26]), .C_i(add_1bit_28_c_1_1), .A_i(AA[26]), .R_i(RR[26]), .C_1_1(add_1bit_31_c_1_1));

  // Other names for the same wires on the sheet: A0 = AA[0]; A1 = AA[1]; A2 = AA[2]; A3 = AA[3]; A4 = AA[4];
  //   A5 = AA[5]; A6 = AA[6]; A7 = AA[7]; A8 = AA[8]; A9 = AA[9]; A10 = AA[10]; A11 = AA[11]; A12 = AA[12];
  //   A13 = AA[13]; A14 = AA[14]; A15 = AA[15]; A16 = AA[16]; A17 = AA[17]; A18 = AA[18]; A19 = AA[19]; A20 = AA[20];
  //   A21 = AA[21]; A22 = AA[22]; A23 = AA[23]; A24 = AA[24]; A25 = AA[25]; A26 = AA[26]; A27 = AA[27]; A28 = AA[28];
  //   A29 = AA[29]; A30 = AA[30]; A31 = AA[31]; B0 = BB[0]; B1 = BB[1]; B2 = BB[2]; B3 = BB[3]; B4 = BB[4];
  //   B5 = BB[5]; B6 = BB[6]; B7 = BB[7]; B8 = BB[8]; B9 = BB[9]; B10 = BB[10]; B11 = BB[11]; B12 = BB[12];
  //   B13 = BB[13]; B14 = BB[14]; B15 = BB[15]; B16 = BB[16]; B17 = BB[17]; B18 = BB[18]; B19 = BB[19]; B20 = BB[20];
  //   B21 = BB[21]; B22 = BB[22]; B23 = BB[23]; B24 = BB[24]; B25 = BB[25]; B26 = BB[26]; B27 = BB[27]; B28 = BB[28];
  //   B29 = BB[29]; B30 = BB[30]; B31 = BB[31]; R0 = RR[0]; R1 = RR[1]; R2 = RR[2]; R3 = RR[3]; R4 = RR[4];
  //   R5 = RR[5]; R6 = RR[6]; R7 = RR[7]; R8 = RR[8]; R9 = RR[9]; R10 = RR[10]; R11 = RR[11]; R12 = RR[12];
  //   R13 = RR[13]; R14 = RR[14]; R15 = RR[15]; R16 = RR[16]; R17 = RR[17]; R18 = RR[18]; R19 = RR[19]; R20 = RR[20];
  //   R21 = RR[21]; R22 = RR[22]; R23 = RR[23]; R24 = RR[24]; R25 = RR[25]; R26 = RR[26]; R27 = RR[27]; R28 = RR[28];
  //   R29 = RR[29]; R30 = RR[30]; R31 = RR[31]
endmodule

module _1bit_ADDer (
  input  A,
  input  B,
  output R,
  output C
);

  xor xor_1 (R, A, B);
  and and_1 (C, A, B);
endmodule

// SUB
module _32bit_SUBer (
  input  [31:0] AA_sub,
  input  [31:0] BB_sub,
  output [31:0] RR_sub
);

  wire [31:0] n32bit_adder_1_rr, not_1_out;

  assign not_1_out = ~BB_sub;  // NOT_Gate not_1, 32 bits wide
  _32bit_ADDer u_32bit_adder_1 (.AA(not_1_out), .BB(32'h1), .RR(n32bit_adder_1_rr));
  _32bit_ADDer u_32bit_adder_2 (.AA(AA_sub), .BB(n32bit_adder_1_rr), .RR(RR_sub));
endmodule

module ALU (
  input  [31:0] in_ALU_1,
  input  [31:0] in_ALU_2,
  input  [1:0] ALUctr,
  input  beq,
  output ZERO,
  output [31:0] out_ALU
);

  wire nor_1_out;
  wire [31:0] n32bit_adder_1_rr, n32bit_suber_1_rr_sub, or_1_out;

  _32bit_ADDer u_32bit_adder_1 (.AA(in_ALU_1), .BB(in_ALU_2), .RR(n32bit_adder_1_rr));
  _32bit_SUBer u_32bit_suber_1 (.AA_sub(in_ALU_1), .BB_sub(in_ALU_2), .RR_sub(n32bit_suber_1_rr_sub));
  assign or_1_out = in_ALU_1 | in_ALU_2;  // OR_Gate or_1, 32 bits wide
  Multiplexer #(.select(2), .width(32), .enable("false")) multiplexer_1 (
    .in0(n32bit_adder_1_rr), .in1(n32bit_suber_1_rr_sub), .in2(or_1_out), .out(out_ALU), .sel(ALUctr));  // open: in3
  nor nor_1 (nor_1_out, n32bit_suber_1_rr_sub[0], n32bit_suber_1_rr_sub[1], n32bit_suber_1_rr_sub[2], n32bit_suber_1_rr_sub[3], n32bit_suber_1_rr_sub[4], n32bit_suber_1_rr_sub[5], n32bit_suber_1_rr_sub[6], n32bit_suber_1_rr_sub[7], n32bit_suber_1_rr_sub[8], n32bit_suber_1_rr_sub[9], n32bit_suber_1_rr_sub[10], n32bit_suber_1_rr_sub[11], n32bit_suber_1_rr_sub[12], n32bit_suber_1_rr_sub[13], n32bit_suber_1_rr_sub[14], n32bit_suber_1_rr_sub[15], n32bit_suber_1_rr_sub[17], n32bit_suber_1_rr_sub[18], n32bit_suber_1_rr_sub[19], n32bit_suber_1_rr_sub[20], n32bit_suber_1_rr_sub[21], n32bit_suber_1_rr_sub[22], n32bit_suber_1_rr_sub[23], n32bit_suber_1_rr_sub[24], n32bit_suber_1_rr_sub[25], n32bit_suber_1_rr_sub[26], n32bit_suber_1_rr_sub[27], n32bit_suber_1_rr_sub[28], n32bit_suber_1_rr_sub[29], n32bit_suber_1_rr_sub[30], n32bit_suber_1_rr_sub[31], n32bit_suber_1_rr_sub[16]);
  and and_1 (ZERO, nor_1_out, beq);
endmodule

// EXT
module Extener (
  input  [15:0] in_Extener,
  input  [1:0] ExtOp,
  output [31:0] out_Extener
);

  wire [15:0] demultiplexer_1_out0, demultiplexer_1_out1, demultiplexer_1_out2;
  wire [31:0] bit_extender_1_out, bit_extender_2_out;

  Demultiplexer #(.select(2), .width(16), .enable("false")) demultiplexer_1 (
    .out0(demultiplexer_1_out0), .out1(demultiplexer_1_out1), .out2(demultiplexer_1_out2), .in(in_Extener),
    .sel(ExtOp));  // open: out3
  assign bit_extender_1_out = {{16{1'b0}}, demultiplexer_1_out0};  // Bit_Extender bit_extender_1
  assign bit_extender_2_out = {{16{demultiplexer_1_out1[15]}}, demultiplexer_1_out1};  // Bit_Extender bit_extender_2
  Multiplexer #(.select(2), .width(32), .enable("false")) multiplexer_1 (
    .in0(bit_extender_1_out), .in1(bit_extender_2_out), .in2({demultiplexer_1_out2, {16{1'b0}}}),
    .out(out_Extener), .sel(ExtOp));  // open: in3
endmodule

// Con
module Controller (
  input  [5:0] FUNCT,
  input  [5:0] Op,
  output sb,
  output RegDst,
  output ALUSrc,
  output MemtoReg,
  output RegWrite,
  output MemWrite,
  output j,
  output beq,
  output [1:0] ExtOp,
  output [1:0] ALUctr
);

  wire addu_out, lw_out, not_1_out, not_2_out, not_3_out, not_4_out, not_5_out, not_6_out, not_7_out,
       not_8_out, not_9_out, not_10_out, not_11_out, not_12_out, ori_out, subu_out, sw_out;

  not not_1 (not_1_out, FUNCT[5]);
  not not_2 (not_2_out, FUNCT[4]);
  not not_3 (not_3_out, FUNCT[3]);
  not not_4 (not_4_out, FUNCT[1]);
  not not_5 (not_5_out, FUNCT[2]);
  not not_6 (not_6_out, Op[5]);
  not not_7 (not_7_out, FUNCT[0]);
  not not_8 (not_8_out, Op[3]);
  not not_9 (not_9_out, Op[4]);
  not not_10 (not_10_out, Op[1]);
  not not_11 (not_11_out, Op[2]);
  not not_12 (not_12_out, Op[0]);
  and addu (addu_out, not_6_out, not_9_out, not_8_out, not_11_out, not_10_out, not_12_out, FUNCT[5], not_2_out, not_3_out, not_5_out, not_4_out, FUNCT[0]);
  and subu (subu_out, not_6_out, not_9_out, not_8_out, not_11_out, not_10_out, not_12_out, FUNCT[5], not_2_out, not_3_out, not_5_out, FUNCT[1], FUNCT[0]);
  and ori (ori_out, not_6_out, not_9_out, Op[3], Op[2], not_10_out, Op[0]);
  and lw (lw_out, Op[5], not_9_out, not_8_out, not_11_out, Op[1], Op[0]);
  and sw (sw_out, Op[5], not_9_out, Op[3], not_11_out, Op[1], Op[0]);
  and u_beq (beq, not_6_out, not_9_out, not_8_out, Op[2], not_10_out, not_12_out);
  and lui (ExtOp[1], not_6_out, not_9_out, Op[3], Op[2], Op[1], Op[0]);
  and u_j (j, not_6_out, not_9_out, not_8_out, not_11_out, Op[1], not_12_out);
  and u_sb (sb, Op[5], not_9_out, Op[3], not_11_out, not_10_out, not_12_out);
  or u_RegDst (RegDst, addu_out, subu_out);
  or u_ALUSrc (ALUSrc, ori_out, lw_out, sb, sw_out, ExtOp[1]);
  buf u_MemtoReg (MemtoReg, lw_out);  // OR_Gate
  or u_RegWrite (RegWrite, addu_out, subu_out, ori_out, lw_out, ExtOp[1]);
  or u_MemWrite (MemWrite, sw_out, sb);
  or u_ExtOp (ExtOp[0], lw_out, sw_out);
  or ALUctr_1 (ALUctr[1], ori_out, ExtOp[1]);
  or ALUctr_0 (ALUctr[0], subu_out, beq);
endmodule

// GPR
module RegFile (
  input  RegW,
  input  clk,
  input  reset,
  input  [4:0] rs,
  input  [4:0] rt,
  input  [4:0] rw,
  input  [31:0] busW,
  output [31:0] busB,
  output [31:0] busA
);

  wire demultiplexer_1_out0, demultiplexer_1_out1, demultiplexer_1_out2, demultiplexer_1_out3,
       demultiplexer_1_out4, demultiplexer_1_out5, demultiplexer_1_out6, demultiplexer_1_out7,
       demultiplexer_1_out8, demultiplexer_1_out9, demultiplexer_1_out10, demultiplexer_1_out11,
       demultiplexer_1_out12, demultiplexer_1_out13, demultiplexer_1_out14, demultiplexer_1_out15,
       demultiplexer_1_out16, demultiplexer_1_out17, demultiplexer_1_out18, demultiplexer_1_out19,
       demultiplexer_1_out20, demultiplexer_1_out21, demultiplexer_1_out22, demultiplexer_1_out23,
       demultiplexer_1_out24, demultiplexer_1_out25, demultiplexer_1_out26, demultiplexer_1_out27,
       demultiplexer_1_out28, demultiplexer_1_out29, demultiplexer_1_out30, demultiplexer_1_out31;
  wire [31:0] _0, _1, _2, _3, _4, _5, _6, _7, _8, _9, _10, _11, _12, _13, _14, _15, _16, _17, _18, _19, _20,
       _21, _22, _23, _24, _25, _26, _27, _28, _29, _30, _31;

  Demultiplexer #(.select(5)) demultiplexer_1 (
    .out0(demultiplexer_1_out0), .out1(demultiplexer_1_out1), .out2(demultiplexer_1_out2),
    .out3(demultiplexer_1_out3), .out4(demultiplexer_1_out4), .out5(demultiplexer_1_out5),
    .out6(demultiplexer_1_out6), .out7(demultiplexer_1_out7), .out8(demultiplexer_1_out8),
    .out9(demultiplexer_1_out9), .out10(demultiplexer_1_out10), .out11(demultiplexer_1_out11),
    .out12(demultiplexer_1_out12), .out13(demultiplexer_1_out13), .out14(demultiplexer_1_out14),
    .out15(demultiplexer_1_out15), .out16(demultiplexer_1_out16), .out17(demultiplexer_1_out17),
    .out18(demultiplexer_1_out18), .out19(demultiplexer_1_out19), .out20(demultiplexer_1_out20),
    .out21(demultiplexer_1_out21), .out22(demultiplexer_1_out22), .out23(demultiplexer_1_out23),
    .out24(demultiplexer_1_out24), .out25(demultiplexer_1_out25), .out26(demultiplexer_1_out26),
    .out27(demultiplexer_1_out27), .out28(demultiplexer_1_out28), .out29(demultiplexer_1_out29),
    .out30(demultiplexer_1_out30), .out31(demultiplexer_1_out31), .in(RegW), .sel(rw));  // open: en
  Register #(.width(32)) register_1 (.en(demultiplexer_1_out0), .Q(_0), .clk(clk), .clr(reset));  // open: D
  Register #(.width(32)) register_2 (.D(busW), .en(demultiplexer_1_out1), .Q(_1), .clk(clk), .clr(reset));
  Register #(.width(32)) register_3 (.D(busW), .en(demultiplexer_1_out2), .Q(_2), .clk(clk), .clr(reset));
  Register #(.width(32)) register_4 (.D(busW), .en(demultiplexer_1_out3), .Q(_3), .clk(clk), .clr(reset));
  Register #(.width(32)) register_5 (.D(busW), .en(demultiplexer_1_out4), .Q(_4), .clk(clk), .clr(reset));
  Register #(.width(32)) register_6 (.D(busW), .en(demultiplexer_1_out5), .Q(_5), .clk(clk), .clr(reset));
  Register #(.width(32)) register_7 (.D(busW), .en(demultiplexer_1_out6), .Q(_6), .clk(clk), .clr(reset));
  Register #(.width(32)) register_8 (.D(busW), .en(demultiplexer_1_out7), .Q(_7), .clk(clk), .clr(reset));
  Register #(.width(32)) register_9 (.D(busW), .en(demultiplexer_1_out8), .Q(_8), .clk(clk), .clr(reset));
  Register #(.width(32)) register_10 (.D(busW), .en(demultiplexer_1_out9), .Q(_9), .clk(clk), .clr(reset));
  Register #(.width(32)) register_11 (.D(busW), .en(demultiplexer_1_out10), .Q(_10), .clk(clk), .clr(reset));
  Register #(.width(32)) register_12 (.D(busW), .en(demultiplexer_1_out11), .Q(_11), .clk(clk), .clr(reset));
  Register #(.width(32)) register_13 (.D(busW), .en(demultiplexer_1_out12), .Q(_12), .clk(clk), .clr(reset));
  Register #(.width(32)) register_14 (.D(busW), .en(demultiplexer_1_out13), .Q(_13), .clk(clk), .clr(reset));
  Register #(.width(32)) register_15 (.D(busW), .en(demultiplexer_1_out14), .Q(_14), .clk(clk), .clr(reset));
  Register #(.width(32)) register_16 (.D(busW), .en(demultiplexer_1_out15), .Q(_15), .clk(clk), .clr(reset));
  Register #(.width(32)) register_17 (.D(busW), .en(demultiplexer_1_out16), .Q(_16), .clk(clk), .clr(reset));
  Register #(.width(32)) register_18 (.D(busW), .en(demultiplexer_1_out17), .Q(_17), .clk(clk), .clr(reset));
  Register #(.width(32)) register_19 (.D(busW), .en(demultiplexer_1_out18), .Q(_18), .clk(clk), .clr(reset));
  Register #(.width(32)) register_20 (.D(busW), .en(demultiplexer_1_out19), .Q(_19), .clk(clk), .clr(reset));
  Register #(.width(32)) register_21 (.D(busW), .en(demultiplexer_1_out20), .Q(_20), .clk(clk), .clr(reset));
  Register #(.width(32)) register_22 (.D(busW), .en(demultiplexer_1_out21), .Q(_21), .clk(clk), .clr(reset));
  Register #(.width(32)) register_23 (.D(busW), .en(demultiplexer_1_out22), .Q(_22), .clk(clk), .clr(reset));
  Register #(.width(32)) register_24 (.D(busW), .en(demultiplexer_1_out23), .Q(_23), .clk(clk), .clr(reset));
  Register #(.width(32)) register_25 (.D(busW), .en(demultiplexer_1_out24), .Q(_24), .clk(clk), .clr(reset));
  Register #(.width(32)) register_26 (.D(busW), .en(demultiplexer_1_out25), .Q(_25), .clk(clk), .clr(reset));
  Register #(.width(32)) register_27 (.D(busW), .en(demultiplexer_1_out26), .Q(_26), .clk(clk), .clr(reset));
  Register #(.width(32)) register_28 (.D(busW), .en(demultiplexer_1_out27), .Q(_27), .clk(clk), .clr(reset));
  Register #(.width(32)) register_29 (.D(busW), .en(demultiplexer_1_out28), .Q(_28), .clk(clk), .clr(reset));
  Register #(.width(32)) register_30 (.D(busW), .en(demultiplexer_1_out29), .Q(_29), .clk(clk), .clr(reset));
  Register #(.width(32)) register_31 (.D(busW), .en(demultiplexer_1_out30), .Q(_30), .clk(clk), .clr(reset));
  Register #(.width(32)) register_32 (.D(busW), .en(demultiplexer_1_out31), .Q(_31), .clk(clk), .clr(reset));
  Multiplexer #(.select(5), .width(32), .enable("false")) multiplexer_1 (
    .in0(_0), .in1(_1), .in2(_2), .in3(_3), .in4(_4), .in5(_5), .in6(_6), .in7(_7), .in8(_8), .in9(_9),
    .in10(_10), .in11(_11), .in12(_12), .in13(_13), .in14(_14), .in15(_15), .in16(_16), .in17(_17),
    .in18(_18), .in19(_19), .in20(_20), .in21(_21), .in22(_22), .in23(_23), .in24(_24), .in25(_25),
    .in26(_26), .in27(_27), .in28(_28), .in29(_29), .in30(_30), .in31(_31), .out(busB), .sel(rt));
  Multiplexer #(.select(5), .width(32), .enable("false")) multiplexer_2 (
    .in0(_0), .in1(_1), .in2(_2), .in3(_3), .in4(_4), .in5(_5), .in6(_6), .in7(_7), .in8(_8), .in9(_9),
    .in10(_10), .in11(_11), .in12(_12), .in13(_13), .in14(_14), .in15(_15), .in16(_16), .in17(_17),
    .in18(_18), .in19(_19), .in20(_20), .in21(_21), .in22(_22), .in23(_23), .in24(_24), .in25(_25),
    .in26(_26), .in27(_27), .in28(_28), .in29(_29), .in30(_30), .in31(_31), .out(busA), .sel(rs));
endmodule

module IFU (
  input  j,
  input  Zero,
  input  clk,
  input  reset,
  output [31:0] ifu_out
);

  wire [25:0] PC_4;
  wire [29:0] beq1, bit_extender_1_out, multiplexer_1_out, register_1_q;
  wire [29:26] j1;

  Multiplexer #(.select(2), .width(30), .enable("false")) multiplexer_1 (
    .in0({j1, PC_4}), .in1(beq1), .in2({j1, ifu_out[25:0]}), .in3({j1, PC_4}), .out(multiplexer_1_out),
    .sel({j, Zero}));
  Register #(.width(30)) register_1 (.D(multiplexer_1_out), .Q(register_1_q), .clk(clk), .clr(reset));  // open: en
  Adder #(.width(30)) adder_1 (.a(register_1_q), .b(30'h1), .out({j1, PC_4}));  // open: cin, cout
  ROM #(.addrWidth(6), .dataWidth(32)) rom_1 (.addr(register_1_q[5:0]), .data(ifu_out));  // open: sel
  assign bit_extender_1_out = {{14{ifu_out[15]}}, ifu_out[15:0]};  // Bit_Extender bit_extender_1
  Adder #(.width(30)) adder_2 (.a(bit_extender_1_out), .b({j1, PC_4}), .out(beq1));  // open: cin, cout

  // Other names for the same wires on the sheet: j1[25:0] = ifu_out[25:0]; PC_4[29:26] = j1; sel[1:0] = {j, Zero}

  // Notes on the sheet:
  //   nPC_sel:   beq:10;  j:01
  //   contents of rom_1 (hex, n*v repeats v):
  //   34040004 34050004 34080003 aca80000 34080002 aca80004 34080001 aca80008 34080000 aca8000c 34100000
  //   34180001 34190004 12040015 34110001 b99821 12240010 2799023 8e460000 8e670000 34080000 11060006
  //   11070002 1184021 8000c15 e04021 c03821 1003021 ae460000 ae670000 2388821 2799821 8000c10 2188021
  //   8000c0d 3c01ffff 3c02aaaa 8000c25 8000c26
endmodule
